# Fritzing sketch blutetooth car (saved by Fritzing 0.9.3b)

parts:
  Part2 = Arduino Ethernet Shield (Rev3)
  M3 = DC Motor
  M4 = DC Motor
  S4 = H-Bridge with L298N
  S5 = Round Pushbutton
  Part3 = Bluetooth HC-05 Macho
  VCC2 = 4 x AAA Battery Mount

nets:
  N1: Part2.ETH_CS, S4.IN2
  N2: Part2.PWM_D11, S4.IN1
  GND: Part2.GND, Part3.GND, VCC2.-
  N3: Part2.RX/D0, Part3.TXD
  N4: Part2.TX/D1, Part3.RXD
  N5: Part2.PWM_D5, S4.IN4
  N6: Part2.PWM_D6, S4.IN3
  5V: Part2.5V, Part3.VCC
  N7: M3.pin_1, S4.OUT1-Motor1
  N8: M3.pin_2, S4.OUT2-Motor1
  N9: M4.pin_1, S4.OUT4-Motor2
  N10: M4.pin_2, S4.OUT3-Motor2
  N11: S4.12V, S5.leg1
  N12: S5.leg0, VCC2.+

custom parts:
  H-Bridge with L298N: h-bridge
