# Fritzing sketch bai xe thong minh (saved by Fritzing 0.9.3b)

parts:
  Part1 = Arduino Nano (Rev3.0) (ICSP)
  J1 = Basic Servo
  J2 = Basic Servo
  J3 = Basic Servo
  J4 = Basic Servo
  U1 = LM2596 step down module
  VCC1 = 4 x AAA Battery Mount
  Part2 = Adafruit I2C+SPI LCD Backpack [part_number="Adafruit #292"]  # not connected
  LCD2004-I2C1 = LCD2004-I2C  # not connected
  Part3 = RFID-RC522
  Tiny_RTC1 = Tiny RTC  # not connected
  J5 = Infrared Proximity Sensor
  J6 = Infrared Proximity Sensor
  J7 = Infrared Proximity Sensor
  J8 = Infrared Proximity Sensor

nets:
  N1: Part1.D3, J1.pulse
  N2: Part1.D5, J2.pulse
  N3: Part1.D6, J3.pulse
  N4: Part1.D7, Part3.connector14
  N5: Part1.D8, Part3.connector8
  N6: Part1.D9, J4.pulse
  N7: Part1.D11/MOSI, Part3.connector10
  N8: Part1.D12/MISO, Part3.connector11
  5V: Part1.5V, J5.Vcc
  N9: Part1.A3, J8.Vout
  N10: Part1.A2, J7.Vout
  N11: Part1.A1, J6.Vout
  N12: Part1.A0, J5.Vout
  N13: Part1.3V3, Part3.connector15
  N14: Part1.D13/SCK, Part3.connector9
  GND: J1.gnd, U1.IN-, U1.OUT-, VCC1.-, J8.GND
  N15: J1.vcc, U1.OUT+
  N16: U1.IN+, VCC1.+

custom parts:
  LM2596 step down module: LM2596 DC-DC step down power supply module 3 A.
  Adafruit I2C+SPI LCD Backpack: LCD backpacks reduce the number of pins needed to connect to an LCD. LCDs are a fun and easy way to have your microcontroller project talk back to you. Character LCDs are common, and easy to get, available in tons of colors and sizes. We've written tutorials on using character LCDs with an Arduino (or similar microcontroller) but find that the number of pins necessary to control the LCD can be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
  LCD2004-I2C: A standard character display with 4x20 characters. Comes in many colors with LCM2004 IIC attached.
  Tiny RTC: Tiny RTC I2C module DS1370Z RTC and AT24C32 EEPROM
