# Fritzing sketch Untitled Sketch 2 (saved by Fritzing 0.9.3b)

parts:
  U1 = NodeMCU V1.0
  2_Channel_Relay1 = 2 Channel Power Relay
  Part1 = Breakout Board for Electret Microphone

nets:
  N1: U1.D4, Part1.AUD
  GND: U1.GND, Part1.GND
  N2: U1.D5, 2_Channel_Relay1.IN1
  VIN: U1.Vin, Part1.VCC

custom parts:
  NodeMCU V1.0: ESP8266 based NodeMCU
  2 Channel Power Relay: A 2 channel power relay. The module operates at 5V.
