# Fritzing sketch Untitled Sketch 5 (saved by Fritzing 0.9.3b)

parts:
  2_Channel_Relay1 = 2 Channel Power Relay
  LCM1602_IIC1 = LCM1602 IIC [part_number="LCM1602 IIC" chip_label="LCM1602 IIC" package="DIP (Dual Inline) [THT]"]
  U1 = LCD-16X2 [package=lcd-16x2]
  GSM_SIM_GPSR_SMS_SIM900_SIM1 = SIM800L [package=THT]
  Part1 = Arduino Nano (Rev3.0)
  VCC1 = Battery block 9V
  U2 = LM2596 step down module
  S2 = Round Pushbutton
  S3 = Pushbutton [package="[THT]"]
  S4 = Pushbutton [package="[THT]"]

nets:
  N1: 2_Channel_Relay1.IN1, Part1.D5
  N2: 2_Channel_Relay1.IN2, Part1.D4
  VSS: LCM1602_IIC1.VSS, U1.VSS
  VDD: LCM1602_IIC1.VDD, U1.VDD
  N3: LCM1602_IIC1.V0, U1.VO
  N4: LCM1602_IIC1.RS, U1.RS
  N5: LCM1602_IIC1.RW, U1.R_W
  N6: LCM1602_IIC1.E, U1.E
  N7: LCM1602_IIC1.D0, U1.DB0
  N8: LCM1602_IIC1.D1, U1.DB1
  N9: LCM1602_IIC1.D2, U1.DB2
  N10: LCM1602_IIC1.D3, U1.DB3
  N11: LCM1602_IIC1.D4, U1.DB4
  N12: LCM1602_IIC1.D5, U1.DB5
  N13: LCM1602_IIC1.D6, U1.DB6
  N14: LCM1602_IIC1.D7, U1.DB7
  N15: LCM1602_IIC1.A, U1.A
  N16: LCM1602_IIC1.K, U1.K
  VCC: LCM1602_IIC1.VCC, Part1.5V
  N17: LCM1602_IIC1.SDA, Part1.A4
  N18: LCM1602_IIC1.SCL, Part1.A5
  N19: GSM_SIM_GPSR_SMS_SIM900_SIM1.5V, U2.OUT+
  N20: GSM_SIM_GPSR_SMS_SIM900_SIM1.GND, U2.IN-, U2.OUT-
  N21: GSM_SIM_GPSR_SMS_SIM900_SIM1.SIM_TXD, Part1.D2
  N22: GSM_SIM_GPSR_SMS_SIM900_SIM1.SIM_RXD, Part1.D3
  N23: Part1.D6, S3.Pin_3, S3.Pin_4
  N24: Part1.VIN, U2.IN+, S2.leg1
  N25: Part1.GND, VCC1.-
  N26: S3.Pin_1, S3.Pin_2
  N27: S4.Pin_1, S4.Pin_2, S4.Pin_3, S4.Pin_4

custom parts:
  2 Channel Power Relay: A 2 channel power relay. The module operates at 5V.
  LCM1602 IIC: I2C-Module to use a 1602 or 2004 LCD on with the wire.h libory Serial LCD Modul
  LM2596 step down module: LM2596 DC-DC step down power supply module 3 A.
