# Fritzing sketch led (saved by Fritzing 0.9.3b)

parts:
  Part1 = Arduino Uno (Rev3)
  Part2 = Bluetooth HC-05 Macho
  VCC1 = 4 x AAA Battery Mount
  LED1 = smd LED [color="Red (633nm)" package="0805 [SMD]"]  # not connected
  LED2 = smd LED [color="Red (633nm)" package="0805 [SMD]"]  # not connected
  LED3 = smd LED [color="Red (633nm)" package="0805 [SMD]"]  # not connected
  LED4 = smd LED [color="Red (633nm)" package="0805 [SMD]"]
  LED5 = smd LED [color="Red (633nm)" package="0805 [SMD]"]  # not connected
  R1 = Resistor [tolerance=±5% resistance=220 package="0805 [SMD]"]
  R2 = Resistor [tolerance=±5% resistance=220 package="0805 [SMD]"]
  R3 = Resistor [tolerance=±5% resistance=220 package="0805 [SMD]"]
  R4 = Resistor [tolerance=±5% resistance=220 package="0805 [SMD]"]
  R5 = Resistor [tolerance=±5% resistance=220 package="0805 [SMD]"]

nets:
  N1: Part1.D8, R5.Pin_0
  N2: Part1.D9_PWM, R2.Pin_0
  N3: Part1.D10_PWM/SS, R1.Pin_0
  N4: Part1.D11_PWM/MOSI, R4.Pin_0
  N5: Part1.D12/MISO, R3.Pin_0
  GND: Part1.GND, Part2.GND, VCC1.-, LED4.cathode
  N6: Part1.D2, Part2.RXD
  N7: Part1.D3_PWM, Part2.TXD
  5V: Part1.5V, Part2.VCC
  N8: Part1.VIN, VCC1.+
