# Fritzing sketch Untitled Sketch (saved by Fritzing 0.9.3b)

parts:
  WeMos_D1_R1 = WeMos D1 R2
  Display1 = LCD screen 16x2 IIC [part_number=101290]
  Part1 = Soil Moisture Sensor
  R1 = Photocell (LDR) [package=THT]
  YL-83_-_Control_Board1 = YL-83 Rain Sensor - Control Board
  S1 = H-Bridge with L298N
  YL-83_-_Control_Board2 = YL-83 Rain Sensor - Control Board
  S2 = Round Pushbutton
  M1 = DC Motor  # not connected
  RTC1 = DS1307 RTC Breakout  # not connected
  DHT1 = DHT11 Humitidy and Temperature Sensor
  S3 = SWITCH-MOMENTARY-2 [package=tactile-pth-12mm]  # not connected
  KY-1 = Keyes Relay [package=THT]
  C2 = Capacitor Polarized [package=cpol-radial-10uf-25v]  # not connected
  J1 = Power Jack [package=power_jack_pth]

nets:
  N1: WeMos_D1_R1.D3, DHT1.DATA
  N2: WeMos_D1_R1.D4, YL-83_-_Control_Board2.VCC
  N3: WeMos_D1_R1.(D5), YL-83_-_Control_Board1.VCC
  N4: WeMos_D1_R1.(D6), S1.IN2
  N5: WeMos_D1_R1.D8, KY-1.signal
  N6: WeMos_D1_R1.D14, Display1.SDA
  N7: WeMos_D1_R1.D15, Display1.SCL
  N8: WeMos_D1_R1.A0, YL-83_-_Control_Board1.AO
  N9: WeMos_D1_R1.VIN, S2.leg1
  GND: WeMos_D1_R1.GND, Display1.GND
  5V: WeMos_D1_R1.5V, Display1.VCC
  N10: Part1.VCC, YL-83_-_Control_Board1.POS
  N11: Part1.GND, YL-83_-_Control_Board1.NEG
  N12: R1.pin_0, YL-83_-_Control_Board2.NEG
  N13: R1.pin_1, YL-83_-_Control_Board2.POS
  N14: S2.leg0, J1.PWR

custom parts:
  WeMos D1 R2: The D1 R2 is a mini wifi board based on the ESP-8266EX.
  LCD screen 16x2 IIC: LCD screen with HD44780 controller enables showing text, symbols, value or anything else that comes from Croduino/Arduino. It is capable of showing 16 symbols in two lines and therefore can be used in many projects that need to send clearly visible and legible output information.. • Color of symbols: White • Backlight: Blue • Dimensions: 80 x 36 x 12 mm • Screen dimensions: 64.5 x 16 mm •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
  YL-83 Rain Sensor - Control Board: The YL-83 is a rain sensor that has more resistance when dry and less resistance when wet. The module runs at 5V.
  H-Bridge with L298N: h-bridge
  DS1307 RTC Breakout: DS1307 Real-time Clock Breakout Board with Battery
  DHT11 Humitidy and Temperature Sensor: DHT11 Humidity and Temperature Sensor
  Keyes Relay: The Keyes 5V relay module is suitable for SCM development, home appliance control. It uses a 5V~12V TIL control signal which can control DC / AC signal.
