# Fritzing sketch nha thong minh sim 800L (saved by Fritzing 0.9.3b)

parts:
  Part1 = Arduino Uno (Rev3) - ICSP
  M1 = RioRand LM2596
  Part3 = LCD1602-I2C
  S1 = Round Pushbutton
  YL-83_-_Detection_Board1 = YL-83 Rain Sensor - Detection Board
  YL-83_-_Control_Board1 = YL-83 Rain Sensor - Control Board
  R1 = PHOTOCELL [package=photocell-kit]
  YL-83_-_Control_Board2 = YL-83 Rain Sensor - Control Board
  M2 = Stepper Motor - Bipolar
  DRV_1 = DRV 8825 Stepper Motor Carrier, High Current [part_number="DRV 8825"]
  U1 = SWITCH-SPST-2 [package=switch-spst-vertical]
  VCC1 = 4 x AAA Battery Mount
  U2 = SWITCH-SPST-2 [package=switch-spst-vertical]
  DHT1 = DHT11 Humitidy and Temperature Sensor

nets:
  N1: Part1.A4/SDA, Part3.SDA
  N2: Part1.A5/SCL, Part3.SCL
  N3: Part1.D8, DRV_1.DIRECTION
  N4: Part1.D9_PWM, DRV_1.STEP
  N5: Part1.D2, U2.O
  N6: Part1.D3_PWM, YL-83_-_Control_Board2.DO
  N7: Part1.D4, S1.leg1
  N8: Part1.D5_PWM, YL-83_-_Control_Board1.DO
  N9: Part1.D7, DHT1.DATA
  5V: Part1.5V, Part3.VCC
  GND: Part1.GND, Part3.GND
  N10: M1.Pin_1, DRV_1.VOLTAGE_ST/_MT, U1.P
  N11: M1.Pin_2, VCC1.-
  N12: S1.leg0, U2.P
  N13: YL-83_-_Detection_Board1.POS, YL-83_-_Control_Board1.POS
  N14: YL-83_-_Detection_Board1.NEG, YL-83_-_Control_Board1.NEG
  VCC: YL-83_-_Control_Board1.VCC, YL-83_-_Control_Board2.VCC
  GND_2: YL-83_-_Control_Board1.GND, YL-83_-_Control_Board2.GND
  N15: R1.P$1, YL-83_-_Control_Board2.NEG
  N16: R1.P$2, YL-83_-_Control_Board2.POS
  N17: M2.A, DRV_1.OUT_2B
  N18: M2.C, DRV_1.OUT_2A
  N19: M2.B, DRV_1.OUT_1A
  N20: M2.D, DRV_1.OUT_1B
  N21: U1.O, VCC1.+

custom parts:
  LCD1602-I2C: A standard character display, usually with 2x16 characters. Comes in many colors with LCM1602 IIC attached.
  YL-83 Rain Sensor - Detection Board: The YL-83 is a rain sensor that has more resistance when dry and less resistance when wet. The module runs at 5V.
  YL-83 Rain Sensor - Control Board: The YL-83 is a rain sensor that has more resistance when dry and less resistance when wet. The module runs at 5V.
  DHT11 Humitidy and Temperature Sensor: DHT11 Humidity and Temperature Sensor
