# Fritzing sketch follow line car (saved by Fritzing 0.9.3b)

parts:
  M2 = DC Motor
  M1 = DC Motor
  S2 = Square Pushbutton
  VCC1 = 4 x AAA Battery Mount
  J2 = Infrared Proximity Sensor
  J3 = Infrared Proximity Sensor
  J4 = Infrared Proximity Sensor
  J5 = Infrared Proximity Sensor
  Part1 = Arduino Uno (Rev3) - ICSP
  S1 = H-Bridge with L298N
  J1 = Infrared Proximity Sensor
  hc-sr1 = hc-sr04

nets:
  N1: M2.pin_1, S1.OUT4-Motor2
  N2: M2.pin_2, S1.OUT3-Motor2
  N3: M1.pin_1, S1.OUT1-Motor1
  N4: M1.pin_2, S1.OUT2-Motor1
  N5: S2.leg0, S1.12V
  N6: S2.leg1, VCC1.+
  N7: VCC1.-, S1.GND
  N8: J2.Vout, Part1.A1
  N9: J3.Vout, Part1.A2
  N10: J4.Vout, Part1.A3
  GND: J4.GND, Part1.GND, J1.GND
  VCC: J4.Vcc, Part1.5V
  N11: J5.Vout, Part1.A4/SDA
  GND_2: J5.GND, hc-sr1.GND
  VCC_2: J5.Vcc, hc-sr1.VCC
  N12: Part1.A0, J1.Vout
  N13: Part1.D9_PWM, S1.IN3
  N14: Part1.D10_PWM/SS, S1.IN2
  N15: Part1.D11_PWM/MOSI, S1.IN1
  N16: Part1.D4, hc-sr1.Echo
  N17: Part1.D5_PWM, hc-sr1.Trig
  N18: Part1.D6_PWM, S1.IN4

custom parts:
  H-Bridge with L298N: h-bridge
