# Fritzing sketch Fritzing (saved by Fritzing 0.9.3b)

parts:
  Part2 = Bluetooth HC-05 Macho
  M2 = DC Motor
  S1 = H-Bridge with L298N
  M1 = DC Motor
  VCC1 = 4 x AAA Battery Mount
  S2 = Round Pushbutton
  Part1 = Arduino Ethernet Shield (Rev3)

nets:
  N1: Part2.TXD, Part1.RX/D0
  N2: Part2.RXD, Part1.TX/D1
  VCC: Part2.VCC, Part1.5V
  GND: Part2.GND, Part1.GND
  N3: M2.pin_1, S1.OUT4-Motor2
  N4: M2.pin_2, S1.OUT3-Motor2
  N5: S1.GND, VCC1.-
  N6: S1.5V, S2.leg1
  N7: S1.IN1, Part1.PWM_D11
  N8: S1.IN2, Part1.ETH_CS
  N9: S1.IN3, Part1.PWM_D6
  N10: S1.IN4, Part1.PWM_D5
  N11: S1.OUT1-Motor1, M1.pin_1
  N12: S1.OUT2-Motor1, M1.pin_2
  N13: VCC1.+, S2.leg0

custom parts:
  H-Bridge with L298N: h-bridge
