# Fritzing sketch thuy canh (saved by Fritzing 0.9.3b)

parts:
  U1 = NodeMCU V1.0
  U2 = LCD-16X2 [package=lcd-16x2]
  LCM1602_IIC1 = LCM1602 IIC [part_number="LCM1602 IIC" chip_label="LCM1602 IIC" package="DIP (Dual Inline) [THT]"]
  Part1 = Soil Moisture Sensor
  DHT1 = DHT11_Temperature_and_Humitidy_Sensor
  Part2 = adafruit [part_number="Adafruit #264"]  # not connected
  U3 = LM2596 step down module
  J1 = Power Plug
  J2 = Piezo Speaker
  2_Channel_Relay1 = 2 Channel Power Relay
  S1 = PH meter [package=THT]

nets:
  N1: U1.D0, 2_Channel_Relay1.JD-VCC
  N2: U1.D1, LCM1602_IIC1.SCL
  N3: U1.D2, LCM1602_IIC1.SDA
  N4: U1.D6, DHT1.connector3
  N5: U1.D7, Part1.SIG
  GND: U1.GND, U3.IN-, U3.OUT-, J1.GND, J1.tip_GND
  VIN: U1.Vin, U3.OUT+, J2.pin2, 2_Channel_Relay1.VCC, S1.pin2
  N6: U1.A0, S1.pin1
  VSS: U2.VSS, LCM1602_IIC1.VSS
  VDD: U2.VDD, LCM1602_IIC1.VDD
  N7: U2.VO, LCM1602_IIC1.V0
  N8: U2.RS, LCM1602_IIC1.RS
  N9: U2.R_W, LCM1602_IIC1.RW
  N10: U2.E, LCM1602_IIC1.E
  N11: U2.DB0, LCM1602_IIC1.D0
  N12: U2.DB1, LCM1602_IIC1.D1
  N13: U2.DB2, LCM1602_IIC1.D2
  N14: U2.DB3, LCM1602_IIC1.D3
  N15: U2.DB4, LCM1602_IIC1.D4
  N16: U2.DB5, LCM1602_IIC1.D5
  N17: U2.DB6, LCM1602_IIC1.D6
  N18: U2.DB7, LCM1602_IIC1.D7
  N19: U2.A, LCM1602_IIC1.A
  N20: U2.K, LCM1602_IIC1.K
  N21: U3.IN+, J1.PWR, J1.tip_PWR

custom parts:
  NodeMCU V1.0: ESP9266 based NodeMCU
  LCM1602 IIC: I2C-Module to use a 1602 or 2004 LCD on with the wire.h libory Serial LCD Modul
  LM2596 step down module: LM2596 DC-DC step down power supply module 3 A.
  Power Plug: Power Jack This is the standard 5.5mm barrel plug for power. This part has bendable leads (i.e. wires in the real world) to connect to wall warts or the breadboard in the standard wire end, and hidden connectors on the tip end that will connect when "plugged in" (overlapped with the jack so it appears "plugged in" in breadboard) to the modified coax jack part. Internal busses connect the two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
  2 Channel Power Relay: A 2 channel power relay. The module operates at 5V.
