# Fritzing sketch khoi project (saved by Fritzing 0.9.3b)

parts:
  Part2 = LCD1602-I2C  # not connected
  R2 = Photocell (LDR) [package=THT]
  YL-83_-_Control_Board1 = YL-83 Rain Sensor - Control Board
  DHT1 = DHT11 Humitidy and Temperature Sensor
  J1 = Power Jack [package=power_jack_pth_lock]
  S4 = Square Pushbutton
  Part3 = Real Time Clock Module - DS1307 RTC Breakout Board
  R3 = Resistor [tolerance=±5% resistance=220 package="0805 [SMD]"]
  JP2 = Header 2 [package=screwterminal-3.5mm-2_lock]
  U3 = TRIAC [package=to-92]
  U4 = MOC3031-M [package=dil06]
  R4 = Resistor [tolerance=±5% resistance=220 package="0805 [SMD]"]
  F1 = Fan - Ventilador [package=THT]
  U6 = L9110 H-bridge module [part_number="L9110 H-bridge"]
  J2 = Basic Servo
  LED1 = LEDs [package=led10mm]
  R5 = Resistor [tolerance=±5% resistance=220 package="0805 [SMD]"]
  S5 = Round Pushbutton
  U7 = NodeMCU V1.0

nets:
  N1: R2.pin_0, YL-83_-_Control_Board1.NEG
  N2: R2.pin_1, YL-83_-_Control_Board1.POS
  N3: YL-83_-_Control_Board1.AO, U7.A0
  N4: DHT1.DATA, U7.D5
  N5: J1.PWR, S4.leg0
  N6: Part3.SCL, U7.D1
  N7: Part3.SDA, U7.D2
  N8: R3.Pin_0, U7.D7
  N9: R3.Pin_1, U4.1
  N10: JP2.1, R5.Pin_0
  N11: JP2.2, LED1.A
  N12: U3.M2, U4.4, R4.Pin_1
  GND: U4.2, U6.GND, J2.gnd
  N13: U4.6, R5.Pin_1
  N14: R4.Pin_0, LED1.C, S5.leg0
  N15: F1.5V, U6.MOTOR_B-B
  N16: F1.GND, U6.MOTOR_B-A
  N17: U6.B-IA, U7.D3

custom parts:
  LCD1602-I2C: A standard character display, usually with 2x16 characters. Comes in many colors with LCM1602 IIC attached.
  YL-83 Rain Sensor - Control Board: The YL-83 is a rain sensor that has more resistance when dry and less resistance when wet. The module runs at 5V.
  DHT11 Humitidy and Temperature Sensor: DHT11 Humidity and Temperature Sensor
  Fan - Ventilador: Ventilador de 2 pines, se encuentra comunmente en computadoras de escritorio
  LEDs: LEDs Standard schematic elements and footprints for 5mm, 3mm, 1206, and 0603 sized LEDs. 5mm - Spark Fun Electronics SKU : COM-00529 (and others)
  NodeMCU V1.0: ESP8266 based NodeMCU
